# Fritzing sketch sketch (saved by Fritzing 0.9.3b)

parts:
  WeMos_D1_Mini1 = WeMos D1 Mini
  OLED1 = OLED 128x64 I2C Monochrome Display
  S4 = Momentary Switch [package=ksa_sealed_tac_switch]
  S5 = Momentary Switch [package=ksa_sealed_tac_switch]
  S6 = Momentary Switch [package=ksa_sealed_tac_switch]
  WeMos_D1_Mini_Battery_Shield1 = WeMos D1 Mini Battery Shield  # not connected
  U1 = SWITCH-SPST-2 [package=switch-spst-vertical]
  U2 = LIPO-110mAh [package=lipo-110]
  J1 = JST XH 2A male [form="♂ (male)" package=THT]

nets:
  5V: WeMos_D1_Mini1.5V, OLED1.VDD
  N1: WeMos_D1_Mini1.D1, OLED1.SDA
  N2: WeMos_D1_Mini1.D2, OLED1.SCK
  N3: WeMos_D1_Mini1.D5, S6.4
  N4: WeMos_D1_Mini1.D6, S5.2
  N5: WeMos_D1_Mini1.D7, S4.2
  N6: WeMos_D1_Mini1.G, OLED1.GND, S4.3, S5.3, S6.3
  N7: U1.O, J1.pin1
  N8: U1.P, U2.+
  N9: U2.-, J1.pin2

custom parts:
  JST XH 2A male: JST XH-2A
